# Fritzing sketch woodsMechanicsDiagram (saved by Fritzing 0.9.3b)
breadboards: 1

parts:
  Part1 = Arduino Uno (Rev3)
  IC1 = ULN2003A [package="SO16 [SMD]"]
  M1 = Stepper Motor - Unipolar
  IC2 = ULN2003A [package="SO16 [SMD]"]
  M2 = Stepper Motor - Unipolar
  S1 = SWITCH-MOMENTARY-2 [package=tactile_switch_smd-2]
  S2 = SWITCH-MOMENTARY-2 [package=tactile_switch_smd-2]
  Part2 = FemtoBuck LED Driver
  S5 = SWITCH-MOMENTARY-2 [package=tactile_switch_smd-2]
  S6 = SWITCH-MOMENTARY-2 [package=tactile_switch_smd-2]
  Part4 = FemtoBuck LED Driver
  LED1 = LEDs [package=led10mm]
  LED2 = LEDs [package=led10mm]
  R1 = Resistor [tolerance=±5% resistance=220 package=THT]
  R2 = Resistor [tolerance=±5% resistance=220 package=THT]
  R3 = Resistor [tolerance=±5% resistance=220 package=THT]
  R4 = Resistor [tolerance=±5% resistance=220 package=THT]

nets:
  N1: Part1.A0, Part4.D+
  N2: Part1.A1, IC2.In_1
  N3: Part1.A2, IC2.In_2
  N4: Part1.A3, IC2.In_3
  N5: Part1.A4/SDA, IC2.In_4
  N6: Part1.D8, S1.1, R2.Pin_1
  N7: Part1.D9_PWM, S6.1, R3.Pin_1
  N8: Part1.D10_PWM/SS, S5.1, R4.Pin_1
  N9: Part1.GND, Part2.D-, Part4.D-, R1.Pin_0, R2.Pin_0, R3.Pin_0, R4.Pin_0
  N10: Part1.D2, Part2.D+
  N11: Part1.D3_PWM, IC1.In_1
  N12: Part1.D4, IC1.In_2
  N13: Part1.D5_PWM, IC1.In_3
  N14: Part1.D6_PWM, IC1.In_4
  N15: Part1.D7, S2.1, R1.Pin_1
  N16: Part1.5V, S1.2, S2.2, S5.2, S6.2
  N17: IC1.Out_6, M1.D
  N18: IC1.Out_5, M1.COMMON_2
  N19: IC1.Out_4, M1.B
  N20: IC1.Out_3, M1.C
  N21: IC1.Out_2, M1.COMMON_1
  N22: IC1.Out_1, M1.A
  N23: IC2.Out_6, M2.D
  N24: IC2.Out_5, M2.COMMON_2
  N25: IC2.Out_4, M2.B
  N26: IC2.Out_3, M2.C
  N27: IC2.Out_2, M2.COMMON_1
  N28: IC2.Out_1, M2.A
  N29: Part2.OUT+, LED2.C
  N30: Part2.OUT-, LED2.A
  N31: Part4.OUT+, LED1.C
  N32: Part4.OUT-, LED1.A
